# Fritzing sketch arduino-window-sensor (saved by Fritzing 0.9.3b)
breadboards: 1

parts:
  WeMos_D1_Mini1 = WeMos D1 Mini
  U6 = TMP36 [package=to-92-kit]
  U7 = HC-SR04 [chip_label=IC package="SIP (Single Inline) [THT]"]
  U8 = HC-SR04 [chip_label=IC package="SIP (Single Inline) [THT]"]
  DHT2 = DHT11 Humitidy and Temperature Sensor

nets:
  3V3: WeMos_D1_Mini1.3V3, U6.VOUT, DHT2.VDD
  VCC: WeMos_D1_Mini1.5V, U7.Vcc, U8.Vcc
  N1: WeMos_D1_Mini1.A0, U6.VCC
  N2: WeMos_D1_Mini1.D1, U7.Trig
  N3: WeMos_D1_Mini1.D2, U7.Echo
  N4: WeMos_D1_Mini1.D3, DHT2.DATA, DHT2.NULL
  N5: WeMos_D1_Mini1.D5, U8.Trig
  N6: WeMos_D1_Mini1.D6, U8.Echo
  GND: WeMos_D1_Mini1.G, U6.GND, U7.GND, U8.GND, DHT2.GND

custom parts:
  HC-SR04: HC-SR04 ultrasound distance sensor
  DHT11 Humitidy and Temperature Sensor: DHT11 Humidity and Temperature Sensor
